// Logisim project Five.circ as structural Verilog: 1 circuit, main circuit main
module main (
  input  Carry_input,
  input  Pin_1,
  input  Pin_2
);

  wire and_1_out, and_2_out, or_1_out, xor_1_out, xor_2_out;

  xor xor_1 (xor_1_out, Pin_1, Pin_2);
  and and_1 (and_1_out, Pin_1, Pin_2);
  xor xor_2 (xor_2_out, Carry_input, xor_1_out);
  and and_2 (and_2_out, xor_1_out, Carry_input);
  LED Sum (.in(xor_2_out));
  or or_1 (or_1_out, and_2_out, and_1_out);
  LED Carry (.in(or_1_out));
endmodule
