// Logisim project Four.circ as structural Verilog: 1 circuit, main circuit main
module main (
  input  Pin_1,
  input  Pin_2
);

  wire and_1_out, xor_1_out;

  xor xor_1 (xor_1_out, Pin_1, Pin_2);
  and and_1 (and_1_out, Pin_1, Pin_2);
  LED Sum_output (.in(xor_1_out));
  LED Carry_output (.in(and_1_out));
endmodule
