// Logisim project One.circ as structural Verilog: 1 circuit, main circuit main
module main (
  input  Pin_1,
  input  Pin_2
);

  wire and_1_out;

  and and_1 (and_1_out, Pin_1, Pin_2);
  LED led_1 (.in(and_1_out));
endmodule
