// Logisim project Three.circ as structural Verilog: 1 circuit, main circuit main
module main (
  input  Pin_1,
  input  Pin_2
);

  wire nand_1_out;

  nand nand_1 (nand_1_out, Pin_1, Pin_2);
  LED led_1 (.in(nand_1_out));
endmodule
