// Logisim project 3.1.circ as structural Verilog: 1 circuit, main circuit main
module main (
  input  D,
  input  S,
  input  E,
  input  R,
  output out_5
);

  wire clock_1_out;

  Clock clock_1 (.out(clock_1_out));
  D_Flip_Flop #(.trigger("falling")) d_ff_1 (
    .clk(clock_1_out), .D(D), .Q(out_5), .preset(S), .en(E), .reset(R));  // open: Qn
endmodule
