// Logisim project 3.2.circ as structural Verilog: 1 circuit, main circuit main
module main (
  input  in_1,
  input  in_2
);

  wire and_1_out, clock_1_out, not_1_out;
  wire [2:0] j_k_ff_1_q;

  Clock clock_1 (.out(clock_1_out));
  J_K_Flip_Flop #(.trigger("falling")) j_k_ff_1 (
    .J(in_1), .clk(clock_1_out), .K(in_1), .Q(j_k_ff_1_q[0]), .reset(and_1_out));  // open: Qn, preset, en
  J_K_Flip_Flop #(.trigger("falling")) j_k_ff_2 (
    .J(in_1), .clk(j_k_ff_1_q[0]), .K(in_1), .Q(j_k_ff_1_q[1]), .reset(and_1_out));  // open: Qn, preset, en
  J_K_Flip_Flop #(.trigger("falling")) j_k_ff_3 (
    .J(in_1), .clk(j_k_ff_1_q[1]), .K(in_1), .Q(j_k_ff_1_q[2]), .reset(and_1_out));  // open: Qn, preset, en
  not not_1 (not_1_out, j_k_ff_1_q[0]);
  and and_1 (and_1_out, j_k_ff_1_q[2], j_k_ff_1_q[1], not_1_out);
  Hex_Digit_Display hex_digit_display_1 (.value({in_2, j_k_ff_1_q}));  // open: dp
endmodule
