// Logisim project 3.4.circ as structural Verilog: 1 circuit, main circuit main
module main (
  input  Data,
  input  in_2,
  input  in_3,
  input  in_4,
  input  Reset,
  output _8,
  output _4,
  output _2,
  output _1
);

  wire Clock_out;

  Clock Clock (.out(Clock_out));
  D_Flip_Flop d_ff_1 (.clk(Clock_out), .D(Data), .Q(_8), .reset(Reset));  // open: Qn, preset, en
  D_Flip_Flop d_ff_2 (.clk(Clock_out), .D(in_2), .Q(_4), .reset(Reset));  // open: Qn, preset, en
  D_Flip_Flop d_ff_3 (.clk(Clock_out), .D(in_3), .Q(_2), .reset(Reset));  // open: Qn, preset, en
  D_Flip_Flop d_ff_4 (.clk(Clock_out), .D(in_4), .Q(_1), .reset(Reset));  // open: Qn, preset, en
endmodule
